# Fritzing sketch lumiere_jour_nuit_generique (saved by Fritzing 0.9.3b)
breadboards: 1

parts:
  RS485_module1 = RS485 Module (MAX3485)
  Composant1 = Arduino Nano (Rev3.0)
  LED1 = LED - 3mm [color="Red (633nm)" package="3 mm [THT]"]
  LED2 = LED - 3mm [color="Yellow (585nm)" package="3 mm [THT]"]
  LED3 = LED - 3mm [color="White (6500K)" package="3 mm [THT]"]
  R2 = Resistor [tolerance=±5% resistance=220 package=THT]
  R3 = Resistor [tolerance=±5% resistance=220 package=THT]
  R4 = Resistor [tolerance=±5% resistance=220 package=THT]

nets:
  GND: RS485_module1.GND, Composant1.GND, R2.Pin_1, R3.Pin_1, R4.Pin_1
  VCC: RS485_module1.VCC, Composant1.5V
  N1: RS485_module1.RO, Composant1.D2
  N2: RS485_module1.RE, RS485_module1.DE, Composant1.A4
  N3: RS485_module1.DI, Composant1.A5
  N4: Composant1.D3, LED3.anode
  N5: Composant1.D4, LED1.anode
  N6: Composant1.D5, LED2.anode
  N7: LED1.cathode, R2.Pin_0
  N8: LED2.cathode, R3.Pin_0
  N9: LED3.cathode, R4.Pin_0

custom parts:
  RS485 Module (MAX3485): Commercially available RS485 to RS232 TTL Module
